// Logisim project 9213010806任晨玮.circ as structural Verilog: 11 circuits, main circuit ◇海明解码
// 海明编码
module \海明编码  (
  input  [15:0] \原始数据 ,
  output [21:0] \海明码 
);

  xor xor_1 (\海明码 [0], \原始数据 [0], \原始数据 [1], \原始数据 [3], \原始数据 [4], \原始数据 [6], \原始数据 [8], \原始数据 [10], \原始数据 [11], \原始数据 [13], \原始数据 [15]);
  xor xor_2 (\海明码 [1], \原始数据 [0], \原始数据 [2], \原始数据 [3], \原始数据 [5], \原始数据 [6], \原始数据 [9], \原始数据 [10], \原始数据 [12], \原始数据 [13]);
  xor xor_3 (\海明码 [3], \原始数据 [1], \原始数据 [2], \原始数据 [3], \原始数据 [7], \原始数据 [8], \原始数据 [9], \原始数据 [10], \原始数据 [14], \原始数据 [15]);
  xor xor_4 (\海明码 [7], \原始数据 [4], \原始数据 [5], \原始数据 [6], \原始数据 [7], \原始数据 [8], \原始数据 [9], \原始数据 [10]);
  xor xor_5 (\海明码 [15], \原始数据 [11], \原始数据 [12], \原始数据 [13], \原始数据 [14], \原始数据 [15]);
  xor xor_6 (\海明码 [21], \海明码 [0], \海明码 [1], \原始数据 [0], \海明码 [3], \原始数据 [1], \原始数据 [2], \原始数据 [3], \海明码 [7], \原始数据 [4], \原始数据 [5], \原始数据 [6], \原始数据 [7], \原始数据 [8], \原始数据 [9], \原始数据 [10], \海明码 [15], \原始数据 [11], \原始数据 [12], \原始数据 [13], \原始数据 [14], \原始数据 [15]);

  assign {\海明码 [20:16], \海明码 [14:8], \海明码 [6:4], \海明码 [2]} = \原始数据 ;

  // Other names for the same wires on the sheet: D12 = \原始数据 [11]; Data[15:0] = \原始数据 ; D14 = \原始数据 [13];
  //   D15 = \原始数据 [14]; D16 = \原始数据 [15]; P1 = \海明码 [0]; P2 = \海明码 [1]; D1 = \原始数据 [0]; P3 = \海明码 [3]; D2 = \原始数据 [1];
  //   D3 = \原始数据 [2]; D4 = \原始数据 [3]; P4 = \海明码 [7]; D5 = \原始数据 [4]; D6 = \原始数据 [5]; D7 = \原始数据 [6]; D8 = \原始数据 [7];
  //   D9 = \原始数据 [8]; D10 = \原始数据 [9]; D11 = \原始数据 [10]; P5 = \海明码 [15]; D13 = \原始数据 [12]; P6 = \海明码 [21]

  // Notes on the sheet:
  //   输入引脚区
  //   请勿增改引脚，请勿修改子电路封装
  //   电路功能：海明编码电路，可检两位错并纠一位错，输入：16位；输出：22位海明码（数据位+校验位）
  //   请在下方利用上方输入输出引脚的隧道信号构建电路，ctrl+d复制选择部件
  //   输出引脚区
endmodule

// 海明解码
module \海明解码  (
  input  [21:0] \海明码 ,
  output \_0位错 ,
  output \_1位错 ,
  output \_2位错 ,
  output [15:0] \纠错后数据 ,
  output [4:0] \纠错后数据_2 
);

  wire and_1_out, and_2_out, decoder_1_out0, G6_out;
  wire [21:0] decoder_1_out1, xor_1_out;

  xor G1 (\纠错后数据_2 [0], \海明码 [2], \海明码 [4], \海明码 [6], \海明码 [8], \海明码 [10], \海明码 [12], \海明码 [14], \海明码 [16], \海明码 [18], \海明码 [20], \海明码 [0]);
  xor G2 (\纠错后数据_2 [1], \海明码 [2], \海明码 [5], \海明码 [6], \海明码 [9], \海明码 [10], \海明码 [13], \海明码 [14], \海明码 [17], \海明码 [18], \海明码 [1]);
  xor G3 (\纠错后数据_2 [2], \海明码 [4], \海明码 [5], \海明码 [6], \海明码 [11], \海明码 [12], \海明码 [13], \海明码 [14], \海明码 [19], \海明码 [20], \海明码 [3]);
  xor G4 (\纠错后数据_2 [3], \海明码 [8], \海明码 [9], \海明码 [10], \海明码 [11], \海明码 [12], \海明码 [13], \海明码 [14], \海明码 [7]);
  xor G5 (\纠错后数据_2 [4], \海明码 [16], \海明码 [17], \海明码 [18], \海明码 [19], \海明码 [20], \海明码 [15]);
  Decoder #(.select(5), .enable("false")) decoder_1 (
    .out0(decoder_1_out0), .out1(decoder_1_out1[0]), .out2(decoder_1_out1[1]), .out3(decoder_1_out1[2]),
    .out4(decoder_1_out1[3]), .out5(decoder_1_out1[4]), .out6(decoder_1_out1[5]), .out7(decoder_1_out1[6]),
    .out8(decoder_1_out1[7]), .out9(decoder_1_out1[8]), .out10(decoder_1_out1[9]),
    .out11(decoder_1_out1[10]), .out12(decoder_1_out1[11]), .out13(decoder_1_out1[12]),
    .out14(decoder_1_out1[13]), .out15(decoder_1_out1[14]), .out16(decoder_1_out1[15]),
    .out17(decoder_1_out1[16]), .out18(decoder_1_out1[17]), .out19(decoder_1_out1[18]),
    .out20(decoder_1_out1[19]), .out21(decoder_1_out1[20]), .out22(decoder_1_out1[21]), .sel(\纠错后数据_2 ));  // open: out23, out24, out25, out26, out27, out28, out29, out30, out31
  xnor G6 (G6_out, \海明码 [0], \海明码 [1], \海明码 [2], \海明码 [3], \海明码 [4], \海明码 [5], \海明码 [6], \海明码 [7], \海明码 [8], \海明码 [9], \海明码 [10], \海明码 [11], \海明码 [12], \海明码 [13], \海明码 [14], \海明码 [15], \海明码 [16], \海明码 [17], \海明码 [18], \海明码 [19], \海明码 [20], \海明码 [21]);
  assign {xor_1_out[21], \纠错后数据 [15:11], xor_1_out[15], \纠错后数据 [10:4], xor_1_out[7], \纠错后数据 [3:1], xor_1_out[3], \纠错后数据 [0], xor_1_out[1:0]} = decoder_1_out1 ^ \海明码 ;  // XOR_Gate xor_1, 22 bits wide
  and and_1 (and_1_out, ~decoder_1_out0, ~G6_out);  // AND_Gate
  and and_2 (and_2_out, decoder_1_out0, ~G6_out);  // AND_Gate
  and and_3 (\_0位错 , decoder_1_out0, G6_out);
  and and_4 (\_2位错 , ~decoder_1_out0, G6_out);  // AND_Gate
  or or_1 (\_1位错 , and_1_out, and_2_out);

  // Other names for the same wires on the sheet: P1 = \海明码 [0]; P2 = \海明码 [1]; D1 = \海明码 [2]; P3 = \海明码 [3];
  //   D2 = \海明码 [4]; D3 = \海明码 [5]; D4 = \海明码 [6]; P4 = \海明码 [7]; D5 = \海明码 [8]; D6 = \海明码 [9]; D7 = \海明码 [10];
  //   D8 = \海明码 [11]; D9 = \海明码 [12]; D10 = \海明码 [13]; D11 = \海明码 [14]; P5 = \海明码 [15]; D12 = \海明码 [16];
  //   D13 = \海明码 [17]; D14 = \海明码 [18]; D15 = \海明码 [19]; D16 = \海明码 [20]; P6 = \海明码 [21]

  // Notes on the sheet:
  //   输入引脚区
  //   输出引脚区
  //   电路功能：
  //   请勿增改引脚，请勿修改子电路封装
  //   输入：22位海明码；输出：纠错后的数据、错误模式
  //   请在下方利用上方输入输出引脚的隧道信号构建电路，ctrl+d复制选择部件
  //   实现22位海明码的数据解码，能判断1位错，2位错，无错误，1位错自动纠错。
endmodule

module \海明传输测试2  (
  input  [1:0] \加扰控制 
);

  wire CLK, comparator_1_eq, \海明解码_1__0位错 , \海明解码_1__1位错 , \海明解码_1__2位错 ;
  wire [6:0] \国标转区位码_1_位号 , \国标转区位码_1_区号 , \国标转区位码_2_位号 , \国标转区位码_2_区号 ;
  wire [7:0] counter_1_q;
  wire [15:0] \发送 , \接收 ;
  wire [21:0] \n22位随机干扰_1_加扰后数据 , \n22位随机干扰_1_随机加扰屏蔽字 , \海明编码_1_海明码 ;
  wire [31:0] \字库_1_out_3 , \字库_1_out_4 , \字库_1_out_5 , \字库_1_out_6 , \字库_1_out_7 , \字库_1_out_8 ,
       \字库_1_out_9 , \字库_1_out_10 , \字库_1_out_11 , \字库_1_out_12 , \字库_1_out_13 , \字库_1_out_14 ,
       \字库_1_out_15 , \字库_1_out_16 , \字库_1_out_17 , \字库_1_out_18 , \字库_1_out_19 , \字库_1_out_20 ,
       \字库_1_out_21 , \字库_1_out_22 , \字库_1_out_23 , \字库_1_out_24 , \字库_1_out_25 , \字库_1_out_26 ,
       \字库_1_out_27 , \字库_1_out_28 , \字库_1_out_29 , \字库_1_out_30 , \字库_1_out_31 , \字库_1_out_32 ,
       \字库_1_out_33 , \字库_1_out_34 , \字库_2_out_3 , \字库_2_out_4 , \字库_2_out_5 , \字库_2_out_6 , \字库_2_out_7 ,
       \字库_2_out_8 , \字库_2_out_9 , \字库_2_out_10 , \字库_2_out_11 , \字库_2_out_12 , \字库_2_out_13 , \字库_2_out_14 ,
       \字库_2_out_15 , \字库_2_out_16 , \字库_2_out_17 , \字库_2_out_18 , \字库_2_out_19 , \字库_2_out_20 ,
       \字库_2_out_21 , \字库_2_out_22 , \字库_2_out_23 , \字库_2_out_24 , \字库_2_out_25 , \字库_2_out_26 ,
       \字库_2_out_27 , \字库_2_out_28 , \字库_2_out_29 , \字库_2_out_30 , \字库_2_out_31 , \字库_2_out_32 ,
       \字库_2_out_33 , \字库_2_out_34 ;

  Counter counter_1 (.Q(counter_1_q), .clk(CLK));  // open: load, D, count, carry, clr
  Clock \u_时钟  (.out(CLK));
  \国标转区位码  \u_国标转区位码_1  (.\位号 (\国标转区位码_1_位号 ), .\区号 (\国标转区位码_1_区号 ), .GB2312(\发送 ));
  \字库  \u_字库_1  (
    .out_3(\字库_1_out_3 ), .out_4(\字库_1_out_4 ), .out_5(\字库_1_out_5 ), .out_6(\字库_1_out_6 ),
    .out_7(\字库_1_out_7 ), .out_8(\字库_1_out_8 ), .out_9(\字库_1_out_9 ), .out_10(\字库_1_out_10 ),
    .out_11(\字库_1_out_11 ), .out_12(\字库_1_out_12 ), .out_13(\字库_1_out_13 ), .out_14(\字库_1_out_14 ),
    .out_15(\字库_1_out_15 ), .out_16(\字库_1_out_16 ), .out_17(\字库_1_out_17 ), .out_18(\字库_1_out_18 ),
    .out_19(\字库_1_out_19 ), .out_20(\字库_1_out_20 ), .out_21(\字库_1_out_21 ), .out_22(\字库_1_out_22 ),
    .out_23(\字库_1_out_23 ), .out_24(\字库_1_out_24 ), .out_25(\字库_1_out_25 ), .out_26(\字库_1_out_26 ),
    .out_27(\字库_1_out_27 ), .out_28(\字库_1_out_28 ), .out_29(\字库_1_out_29 ), .out_30(\字库_1_out_30 ),
    .out_31(\字库_1_out_31 ), .out_32(\字库_1_out_32 ), .out_33(\字库_1_out_33 ), .out_34(\字库_1_out_34 ),
    .\区号 (\国标转区位码_1_区号 ), .\位号 (\国标转区位码_1_位号 ));
  DotMatrix #(.inputtype("row"), .matrixcols(32), .matrixrows(32), .dotshape("circle")) dotmatrix_1 (
    .row0(\字库_1_out_3 ), .row1(\字库_1_out_4 ), .row2(\字库_1_out_5 ), .row3(\字库_1_out_6 ), .row4(\字库_1_out_7 ),
    .row5(\字库_1_out_8 ), .row6(\字库_1_out_9 ), .row7(\字库_1_out_10 ), .row8(\字库_1_out_11 ),
    .row9(\字库_1_out_12 ), .row10(\字库_1_out_13 ), .row11(\字库_1_out_14 ), .row12(\字库_1_out_15 ),
    .row13(\字库_1_out_16 ), .row14(\字库_1_out_17 ), .row15(\字库_1_out_18 ), .row16(\字库_1_out_19 ),
    .row17(\字库_1_out_20 ), .row18(\字库_1_out_21 ), .row19(\字库_1_out_22 ), .row20(\字库_1_out_23 ),
    .row21(\字库_1_out_24 ), .row22(\字库_1_out_25 ), .row23(\字库_1_out_26 ), .row24(\字库_1_out_27 ),
    .row25(\字库_1_out_28 ), .row26(\字库_1_out_29 ), .row27(\字库_1_out_30 ), .row28(\字库_1_out_31 ),
    .row29(\字库_1_out_32 ), .row30(\字库_1_out_33 ), .row31(\字库_1_out_34 ));
  ROM #(.dataWidth(16)) rom_1 (.addr(counter_1_q), .data(\发送 ));  // open: sel
  // Probe on \发送 
  // Probe on \海明编码_1_海明码 
  \海明编码  \u_海明编码_1  (.\原始数据 (\发送 ), .\海明码 (\海明编码_1_海明码 ));
  // Probe on \海明编码_1_海明码 
  // Probe on \n22位随机干扰_1_随机加扰屏蔽字 
  \_22位随机干扰  \u_22位随机干扰_1  (
    .\加扰模式 (\加扰控制 ), .\随机加扰屏蔽字 (\n22位随机干扰_1_随机加扰屏蔽字 ), .\_22位输入 (\海明编码_1_海明码 ), .\加扰后数据 (\n22位随机干扰_1_加扰后数据 ),
    .CLK(CLK));  // open: 增加三位错, EDU
  \国标转区位码  \u_国标转区位码_2  (.\位号 (\国标转区位码_2_位号 ), .\区号 (\国标转区位码_2_区号 ), .GB2312(\接收 ));
  // Probe on \n22位随机干扰_1_加扰后数据 
  // Probe on \n22位随机干扰_1_加扰后数据 
  \字库  \u_字库_2  (
    .out_3(\字库_2_out_3 ), .out_4(\字库_2_out_4 ), .out_5(\字库_2_out_5 ), .out_6(\字库_2_out_6 ),
    .out_7(\字库_2_out_7 ), .out_8(\字库_2_out_8 ), .out_9(\字库_2_out_9 ), .out_10(\字库_2_out_10 ),
    .out_11(\字库_2_out_11 ), .out_12(\字库_2_out_12 ), .out_13(\字库_2_out_13 ), .out_14(\字库_2_out_14 ),
    .out_15(\字库_2_out_15 ), .out_16(\字库_2_out_16 ), .out_17(\字库_2_out_17 ), .out_18(\字库_2_out_18 ),
    .out_19(\字库_2_out_19 ), .out_20(\字库_2_out_20 ), .out_21(\字库_2_out_21 ), .out_22(\字库_2_out_22 ),
    .out_23(\字库_2_out_23 ), .out_24(\字库_2_out_24 ), .out_25(\字库_2_out_25 ), .out_26(\字库_2_out_26 ),
    .out_27(\字库_2_out_27 ), .out_28(\字库_2_out_28 ), .out_29(\字库_2_out_29 ), .out_30(\字库_2_out_30 ),
    .out_31(\字库_2_out_31 ), .out_32(\字库_2_out_32 ), .out_33(\字库_2_out_33 ), .out_34(\字库_2_out_34 ),
    .\区号 (\国标转区位码_2_区号 ), .\位号 (\国标转区位码_2_位号 ));
  LED \u_一位错  (.in(\海明解码_1__1位错 ));
  LED OK (.in(\海明解码_1__0位错 ));
  LED \u_两位错  (.in(\海明解码_1__2位错 ));
  DotMatrix #(.inputtype("row"), .matrixcols(32), .matrixrows(32), .dotshape("circle")) dotmatrix_2 (
    .row0(\字库_2_out_3 ), .row1(\字库_2_out_4 ), .row2(\字库_2_out_5 ), .row3(\字库_2_out_6 ), .row4(\字库_2_out_7 ),
    .row5(\字库_2_out_8 ), .row6(\字库_2_out_9 ), .row7(\字库_2_out_10 ), .row8(\字库_2_out_11 ),
    .row9(\字库_2_out_12 ), .row10(\字库_2_out_13 ), .row11(\字库_2_out_14 ), .row12(\字库_2_out_15 ),
    .row13(\字库_2_out_16 ), .row14(\字库_2_out_17 ), .row15(\字库_2_out_18 ), .row16(\字库_2_out_19 ),
    .row17(\字库_2_out_20 ), .row18(\字库_2_out_21 ), .row19(\字库_2_out_22 ), .row20(\字库_2_out_23 ),
    .row21(\字库_2_out_24 ), .row22(\字库_2_out_25 ), .row23(\字库_2_out_26 ), .row24(\字库_2_out_27 ),
    .row25(\字库_2_out_28 ), .row26(\字库_2_out_29 ), .row27(\字库_2_out_30 ), .row28(\字库_2_out_31 ),
    .row29(\字库_2_out_32 ), .row30(\字库_2_out_33 ), .row31(\字库_2_out_34 ));
  \海明解码  \u_海明解码_1  (
    .\_1位错 (\海明解码_1__1位错 ), .\_2位错 (\海明解码_1__2位错 ), .\_0位错 (\海明解码_1__0位错 ), .\海明码 (\n22位随机干扰_1_加扰后数据 ),
    .\纠错后数据 (\接收 ));  // open: 纠错后数据_2
  // Probe on \接收 
  Comparator #(.width(16)) comparator_1 (.a(\发送 ), .b(\接收 ), .eq(comparator_1_eq));  // open: gt, lt
  LED \u_数据正确  (.in(comparator_1_eq));

  // Notes on the sheet:
  //   发送方
  //   计数器
  //   发送方
  //   汉字显示
  //   GB2312
  //   contents of rom_1 (hex, n*v repeats v):
  //   b4f3 bcd2 bac3 a3a1 ced2 cac7 d4da b6c1 cab1 b3a4 c1bd c4ea b0eb b5c4 bcc6 bfc6 b6fe b0e0 c8ce b3bf
  //   e7e2 a3ac cfb2 bbb6 bca6 a3a8 cef3 a3ac b3aa a3ac ccf8 a3ac a3d2 a3c1 a3d0 a3ac c0ba c7f2 a3ac b9c7
  //   bbd2 bcb6 b0ae c0a4 a3ac d0a1 bada d7d3 d7df bfaa a3a1 d7f7 ceaa d2bb c3fb b0ae bca6 d5e6 b5c4 d2d1
  //   bead c2e9 c4be c1cb a3ac bde2 cacd c3bb d3c3 a3ac c8a5 b7b4 b2b5 b5c3 b5bd b5c4 d6bb bbe1 cac7 d2bb
  //   b6d1 b1ed c7e9 b0fc a3ac b8f9 b1be c3bb c8cb bbe1 d5be d4da c4e3 d5e2 b1df a3ac d5e2 b8f6 cac0 bde7
  //   b3e4 c2fa b6f1 d2e2 a3ac c0a4 c0a4 b5bd b5d7 d4f5 c3b4 b5c3 d7ef c4e3 c3c7 c1cb a3ac ceaa cab2 c3b4
  //   d5e2 d1f9 b6d4 cacc cbfb a1a3 d0a1 bada d7d3 b1f0 b8f8 ced2 c2b6 b3f6 bca6 bdc5 a3a1
  //   Ctrl+T 驱动时钟触发随机干扰变化
  //   发送方在ROM预存了一段中文文字，通过计数器驱动电路每个时钟传输一个汉字到接收方
  //   电路功能：测试海明编解码电路正确性，仿真时设置加扰控制位和原始数据，按CTRL+T触发不同的干扰，检验编解码电路功能
  //   用户实现了国标转区位码电路后，可在中间窗口观察发送方和接收方汉字显示是否一致以观察海明检错纠错性能
  //   海明编解码传输电路
  //   接收方
  //   汉字显示
  //   Ctrl+T 驱动时钟触发随机干扰变化
  //   加扰控制00：不加扰  01:1位加扰 10:2位加扰 11：随机加扰
  //   加扰控制00：不加扰  01:1位加扰 10:2位加扰 11：随机加扰
  //   接收方
  //   请将时钟频率调到8Hz
endmodule

module \海明传输测试1  (
  input  [15:0] \原始数据 ,
  input  [1:0] \加扰控制 
);

  wire clock_1_out, comparator_1_eq, \海明解码_1__0位错 , \海明解码_1__1位错 , \海明解码_1__2位错 ;
  wire [15:0] \海明解码_1_纠错后数据 ;
  wire [21:0] \n22位随机干扰_1_加扰后数据 , \n22位随机干扰_1_随机加扰屏蔽字 , \海明编码_1_海明码 ;

  // Probe on \原始数据 
  // Probe on \海明编码_1_海明码 
  \海明编码  \u_海明编码_1  (.\原始数据 (\原始数据 ), .\海明码 (\海明编码_1_海明码 ));
  // Probe on \海明编码_1_海明码 
  // Probe on \n22位随机干扰_1_随机加扰屏蔽字 
  Clock clock_1 (.out(clock_1_out));
  // Probe on \n22位随机干扰_1_加扰后数据 
  \_22位随机干扰  \u_22位随机干扰_1  (
    .\加扰模式 (\加扰控制 ), .\随机加扰屏蔽字 (\n22位随机干扰_1_随机加扰屏蔽字 ), .\_22位输入 (\海明编码_1_海明码 ), .\加扰后数据 (\n22位随机干扰_1_加扰后数据 ),
    .CLK(clock_1_out));  // open: 增加三位错, EDU
  // Probe on \n22位随机干扰_1_加扰后数据 
  LED OK (.in(\海明解码_1__0位错 ));
  LED \u_两位错  (.in(\海明解码_1__2位错 ));
  LED \u_一位错  (.in(\海明解码_1__1位错 ));
  \海明解码  \u_海明解码_1  (
    .\_1位错 (\海明解码_1__1位错 ), .\_2位错 (\海明解码_1__2位错 ), .\_0位错 (\海明解码_1__0位错 ), .\海明码 (\n22位随机干扰_1_加扰后数据 ),
    .\纠错后数据 (\海明解码_1_纠错后数据 ));  // open: 纠错后数据_2
  // Probe on \海明解码_1_纠错后数据 
  LED \u_数据正确  (.in(comparator_1_eq));
  Comparator #(.width(16)) comparator_1 (.a(\原始数据 ), .b(\海明解码_1_纠错后数据 ), .eq(comparator_1_eq));  // open: gt, lt

  // Notes on the sheet:
  //   发送方
  //   Ctrl+T 驱动时钟触发随机干扰变化
  //   海明编解码传输电路
  //   电路功能：测试海明编解码电路正确性，仿真时设置加扰控制位和原始数据，按CTRL+T触发不同的干扰，检验编解码电路功能
  //   加扰控制00：不加扰  01:1位加扰 10:2位加扰 11：随机加扰
  //   接收方
endmodule

module \国标转区位码  (
  input  [15:0] GB2312,
  output [6:0] \区号 ,
  output [6:0] \位号 
);

  wire [15:7] adder_1_out;

  // Probe on GB2312
  // Probe on \区号 
  Adder #(.width(16)) adder_1 (
    .a(GB2312), .b(16'hdfe0), .out({adder_1_out[15], \区号 , adder_1_out[7], \位号 }));  // open: cin, cout
  // Probe on \位号 

  // Notes on the sheet:
  //   请勿增改引脚，请勿修改子电路封装
  //   输入引脚区
  //   请在下方利用上方输入输出引脚的隧道标签信号构建电路，ctrl+d复制选择组件
  //   华中科技大学计算机学院 计算机组成原理课程组
  //   要求用加法器完成
  //   推荐用最新的logisim意大利hust改良版完成实验，EDU平台采用该版本进行测试
  //   输出引脚区
  //   探测区
endmodule

// 随机干扰
module \_22位随机干扰  (
  input  CLK,
  input  [21:0] \_22位输入 ,
  input  EDU,
  input  [1:0] \加扰模式 ,
  input  \增加三位错 ,
  output [21:0] \随机加扰屏蔽字 ,
  output [21:0] \加扰后数据 
);

  wire comparator_1_eq, \随机信号_5_out ;
  wire [1:0] EDUerr, multiplexer_3_out, \随机信号_4_out ;
  wire [3:0] \随机信号_2_out , \随机信号_3_out , \随机信号_out ;
  wire [7:0] counter_1_q;
  wire [15:0] \_1位加扰A ;
  wire [21:0] \_1位加扰 , \_2位加扰 , \_3位加扰 , multiplexer_1_out, multiplexer_5_out, shifter_1_out, \随机加扰 ;
  wire [21:6] \_1位加扰B , \_1位加扰C ;

  Random #(.width(4)) \u_随机信号  (.clk(CLK), .out(\随机信号_out ));  // open: next, clr
  Decoder #(.select(4), .enable("false")) decoder_1 (
    .out0(\_1位加扰A [0]), .out1(\_1位加扰A [1]), .out2(\_1位加扰A [2]), .out3(\_1位加扰A [3]), .out4(\_1位加扰A [4]),
    .out5(\_1位加扰A [5]), .out6(\_1位加扰A [6]), .out7(\_1位加扰A [7]), .out8(\_1位加扰A [8]), .out9(\_1位加扰A [9]),
    .out10(\_1位加扰A [10]), .out11(\_1位加扰A [11]), .out12(\_1位加扰A [12]), .out13(\_1位加扰A [13]),
    .out14(\_1位加扰A [14]), .out15(\_1位加扰A [15]), .sel(\随机信号_out ));
  Random #(.width(4), .seed(18)) \u_随机信号_2  (.clk(CLK), .out(\随机信号_2_out ));  // open: next, clr
  Decoder #(.select(4), .enable("false")) decoder_2 (
    .out0(\_1位加扰B [6]), .out1(\_1位加扰B [7]), .out2(\_1位加扰B [8]), .out3(\_1位加扰B [9]), .out4(\_1位加扰B [10]),
    .out5(\_1位加扰B [11]), .out6(\_1位加扰B [12]), .out7(\_1位加扰B [13]), .out8(\_1位加扰B [14]), .out9(\_1位加扰B [15]),
    .out10(\_1位加扰B [16]), .out11(\_1位加扰B [17]), .out12(\_1位加扰B [18]), .out13(\_1位加扰B [19]),
    .out14(\_1位加扰B [20]), .out15(\_1位加扰B [21]), .sel(\随机信号_2_out ));
  Random #(.width(4), .seed(3)) \u_随机信号_3  (.clk(CLK), .out(\随机信号_3_out ));  // open: next, clr
  Random #(.width(2), .seed(21)) \u_随机信号_4  (.clk(CLK), .out(\随机信号_4_out ));  // open: next, clr
  Random #(.width(1), .seed(31)) \u_随机信号_5  (.clk(CLK), .out(\随机信号_5_out ));  // open: next, clr
  Decoder #(.select(4), .enable("false")) decoder_3 (
    .out0(\_1位加扰C [6]), .out1(\_1位加扰C [7]), .out2(\_1位加扰C [8]), .out3(\_1位加扰C [9]), .out4(\_1位加扰C [10]),
    .out5(\_1位加扰C [11]), .out6(\_1位加扰C [12]), .out7(\_1位加扰C [13]), .out8(\_1位加扰C [14]), .out9(\_1位加扰C [15]),
    .out10(\_1位加扰C [16]), .out11(\_1位加扰C [17]), .out12(\_1位加扰C [18]), .out13(\_1位加扰C [19]),
    .out14(\_1位加扰C [20]), .out15(\_1位加扰C [21]), .sel(\随机信号_3_out ));
  Pull_Resistor #(.pull(1)) pull_resistor_1 (.node(\加扰模式 ));
  Pull_Resistor pull_resistor_2 (.node(\增加三位错 ));
  Multiplexer #(.width(22), .enable("false")) multiplexer_1 (
    .in0({\_1位加扰B , {6{1'b0}}}), .in1(\_3位加扰 ), .out(multiplexer_1_out), .sel(\增加三位错 ));
  Multiplexer #(.select(2), .width(22), .enable("false")) multiplexer_2 (
    .in0({22{1'b0}}), .in1({{6{1'b0}}, \_1位加扰A }), .in2(\_2位加扰 ), .in3(multiplexer_1_out), .out(\随机加扰 ),
    .sel(\随机信号_4_out ));
  Pull_Resistor pull_resistor_3 (.node(EDU));
  Multiplexer #(.width(2), .enable("false")) multiplexer_3 (
    .in0(\加扰模式 ), .in1(EDUerr), .out(multiplexer_3_out), .sel(EDU));
  Shifter #(.width(22), .shift("rl")) shifter_1 (.in({{6{1'b0}}, \_1位加扰A }), .\dist (5'b00001), .out(shifter_1_out));
  Comparator #(.width(22), .mode("unsigned")) comparator_1 (
    .a({{6{1'b0}}, \_1位加扰A }), .b({\_1位加扰B , {6{1'b0}}}), .eq(comparator_1_eq));  // open: gt, lt
  Multiplexer #(.select(2), .width(22), .enable("false")) multiplexer_4 (
    .in0({22{1'b0}}), .in1(\_1位加扰 ), .in2(\_2位加扰 ), .in3(\随机加扰 ), .out(\随机加扰屏蔽字 ), .sel(multiplexer_3_out));
  Multiplexer #(.width(22), .enable("false")) multiplexer_5 (
    .in0({{6{1'b0}}, \_1位加扰A }), .in1(shifter_1_out), .out(multiplexer_5_out), .sel(comparator_1_eq));
  Counter counter_1 (.Q(counter_1_q), .clk(CLK));  // open: load, D, count, carry, clr
  assign \_2位加扰  = multiplexer_5_out ^ {\_1位加扰B , {6{1'b0}}};  // XOR_Gate xor_1, 22 bits wide
  assign \_3位加扰  = \_2位加扰  ^ {\_1位加扰C , {6{1'b0}}};  // XOR_Gate xor_2, 22 bits wide
  ROM #(.dataWidth(2)) rom_1 (.addr(counter_1_q), .data(EDUerr));  // open: sel
  Multiplexer #(.width(22), .enable("false")) multiplexer_6 (
    .in0(multiplexer_5_out), .in1({\_1位加扰B , {6{1'b0}}}), .out(\_1位加扰 ), .sel(\随机信号_5_out ));
  assign \加扰后数据  = \随机加扰屏蔽字  ^ \_22位输入 ;  // XOR_Gate xor_3, 22 bits wide

  // Notes on the sheet:
  //   在随机加扰模式中增加三位错
  //   两个随机信号分别负责高16位和第16位
  //   22位信道加扰屏蔽字生成电路，加扰模式引脚00：不加扰  01:1位加扰 10:2位加扰 11：0-2位随机加扰
  //   如果两个信号相同，其中一个移位
  //   contents of rom_1 (hex, n*v repeats v):
  //   2 2 1 1 1 4*0 4*2 1 1 1 0 1 0 0 2 0 2 5*0 1 0 1 4*0 2
endmodule

// 随机加扰
module \_17位随机干扰  (
  input  CLK,
  input  [16:0] \_17位输入 ,
  output [16:0] \随机加扰屏蔽字 ,
  output [16:0] \加扰后数据 
);

  wire [4:0] \随机数_2_out , \随机数_3_out , \随机数_out ;
  wire [16:0] or_1_out;
  wire [31:0] decoder_1_out31, decoder_2_out31, decoder_3_out31;

  Decoder #(.select(5), .enable("false")) decoder_1 (
    .out0(decoder_1_out31[31]), .out1(decoder_1_out31[30]), .out2(decoder_1_out31[29]),
    .out3(decoder_1_out31[28]), .out4(decoder_1_out31[27]), .out5(decoder_1_out31[26]),
    .out6(decoder_1_out31[25]), .out7(decoder_1_out31[24]), .out8(decoder_1_out31[23]),
    .out9(decoder_1_out31[22]), .out10(decoder_1_out31[21]), .out11(decoder_1_out31[20]),
    .out12(decoder_1_out31[19]), .out13(decoder_1_out31[18]), .out14(decoder_1_out31[17]),
    .out15(decoder_1_out31[16]), .out16(decoder_1_out31[15]), .out17(decoder_1_out31[14]),
    .out18(decoder_1_out31[13]), .out19(decoder_1_out31[12]), .out20(decoder_1_out31[11]),
    .out21(decoder_1_out31[10]), .out22(decoder_1_out31[9]), .out23(decoder_1_out31[8]),
    .out24(decoder_1_out31[7]), .out25(decoder_1_out31[6]), .out26(decoder_1_out31[5]),
    .out27(decoder_1_out31[4]), .out28(decoder_1_out31[3]), .out29(decoder_1_out31[2]),
    .out30(decoder_1_out31[1]), .out31(decoder_1_out31[0]), .sel(\随机数_out ));
  Random #(.width(5)) \u_随机数  (.clk(CLK), .out(\随机数_out ));  // open: next, clr
  Random #(.width(5), .seed(18)) \u_随机数_2  (.clk(CLK), .out(\随机数_2_out ));  // open: next, clr
  Decoder #(.select(5), .enable("false")) decoder_2 (
    .out0(decoder_2_out31[31]), .out1(decoder_2_out31[30]), .out2(decoder_2_out31[29]),
    .out3(decoder_2_out31[28]), .out4(decoder_2_out31[27]), .out5(decoder_2_out31[26]),
    .out6(decoder_2_out31[25]), .out7(decoder_2_out31[24]), .out8(decoder_2_out31[23]),
    .out9(decoder_2_out31[22]), .out10(decoder_2_out31[21]), .out11(decoder_2_out31[20]),
    .out12(decoder_2_out31[19]), .out13(decoder_2_out31[18]), .out14(decoder_2_out31[17]),
    .out15(decoder_2_out31[16]), .out16(decoder_2_out31[15]), .out17(decoder_2_out31[14]),
    .out18(decoder_2_out31[13]), .out19(decoder_2_out31[12]), .out20(decoder_2_out31[11]),
    .out21(decoder_2_out31[10]), .out22(decoder_2_out31[9]), .out23(decoder_2_out31[8]),
    .out24(decoder_2_out31[7]), .out25(decoder_2_out31[6]), .out26(decoder_2_out31[5]),
    .out27(decoder_2_out31[4]), .out28(decoder_2_out31[3]), .out29(decoder_2_out31[2]),
    .out30(decoder_2_out31[1]), .out31(decoder_2_out31[0]), .sel(\随机数_2_out ));
  Decoder #(.select(5), .enable("false")) decoder_3 (
    .out0(decoder_3_out31[31]), .out1(decoder_3_out31[30]), .out2(decoder_3_out31[29]),
    .out3(decoder_3_out31[28]), .out4(decoder_3_out31[27]), .out5(decoder_3_out31[26]),
    .out6(decoder_3_out31[25]), .out7(decoder_3_out31[24]), .out8(decoder_3_out31[23]),
    .out9(decoder_3_out31[22]), .out10(decoder_3_out31[21]), .out11(decoder_3_out31[20]),
    .out12(decoder_3_out31[19]), .out13(decoder_3_out31[18]), .out14(decoder_3_out31[17]),
    .out15(decoder_3_out31[16]), .out16(decoder_3_out31[15]), .out17(decoder_3_out31[14]),
    .out18(decoder_3_out31[13]), .out19(decoder_3_out31[12]), .out20(decoder_3_out31[11]),
    .out21(decoder_3_out31[10]), .out22(decoder_3_out31[9]), .out23(decoder_3_out31[8]),
    .out24(decoder_3_out31[7]), .out25(decoder_3_out31[6]), .out26(decoder_3_out31[5]),
    .out27(decoder_3_out31[4]), .out28(decoder_3_out31[3]), .out29(decoder_3_out31[2]),
    .out30(decoder_3_out31[1]), .out31(decoder_3_out31[0]), .sel(\随机数_3_out ));
  Random #(.width(5), .seed(3)) \u_随机数_3  (.clk(CLK), .out(\随机数_3_out ));  // open: next, clr
  assign or_1_out = decoder_1_out31[16:0] | decoder_2_out31[16:0];  // OR_Gate or_1, 17 bits wide
  assign \随机加扰屏蔽字  = or_1_out | decoder_3_out31[16:0];  // OR_Gate or_2, 17 bits wide
  assign \加扰后数据  = \随机加扰屏蔽字  ^ \_17位输入 ;  // XOR_Gate xor_1, 17 bits wide
endmodule

module \_22位流水接口  (
  input  [21:0] Din22,
  input  \传输状态In_表明当前传输数据有效 ,
  input  CLK,
  input  \同步清零_气泡_高电平有效 ,
  input  \使能端_低电平有效_stall_高电平有效 ,
  output [21:0] Dout22,
  output \传输状态Out_表明当前传输数据有效 
);

  wire multiplexer_2_out, pull_resistor_2_node;
  wire [21:0] multiplexer_1_out;

  Multiplexer #(.width(22), .enable("false")) multiplexer_1 (
    .in0(Din22), .in1({22{1'b0}}), .out(multiplexer_1_out), .sel(\同步清零_气泡_高电平有效 ));
  Multiplexer #(.enable("false")) multiplexer_2 (
    .in0(\传输状态In_表明当前传输数据有效 ), .in1(1'b0), .out(multiplexer_2_out), .sel(\同步清零_气泡_高电平有效 ));
  Pull_Resistor pull_resistor_1 (.node(\同步清零_气泡_高电平有效 ));
  Register #(.width(22)) register_1 (
    .D(multiplexer_1_out), .en(pull_resistor_2_node), .Q(Dout22), .clk(CLK));  // open: clr
  Register #(.width(1)) register_2 (
    .D(multiplexer_2_out), .en(pull_resistor_2_node), .Q(\传输状态Out_表明当前传输数据有效 ), .clk(CLK));  // open: clr
  Pull_Resistor pull_resistor_2 (.node(pull_resistor_2_node));
  not not_1 (pull_resistor_2_node, \使能端_低电平有效_stall_高电平有效 );

  // Notes on the sheet:
  //   同步清零_气泡_高电平有效: pull=down
  //   使能端_低电平有效_stall_高电平有效: pull=down
endmodule

module \_16位流水接口  (
  input  [15:0] Din16,
  input  \传输状态In_表明当前传输数据有效 ,
  input  CLK,
  input  \同步清零_气泡_高电平有效 ,
  input  \使能端_低电平有效_stall_高电平有效 ,
  output [15:0] Dout16,
  output \传输状态Out_表明当前传输数据有效 
);

  wire multiplexer_2_out, pull_resistor_2_node;
  wire [15:0] multiplexer_1_out;

  Multiplexer #(.width(16), .enable("false")) multiplexer_1 (
    .in0(Din16), .in1({16{1'b0}}), .out(multiplexer_1_out), .sel(\同步清零_气泡_高电平有效 ));
  Multiplexer #(.enable("false")) multiplexer_2 (
    .in0(\传输状态In_表明当前传输数据有效 ), .in1(1'b0), .out(multiplexer_2_out), .sel(\同步清零_气泡_高电平有效 ));
  Pull_Resistor pull_resistor_1 (.node(\同步清零_气泡_高电平有效 ));
  Register #(.width(16)) register_1 (
    .D(multiplexer_1_out), .en(pull_resistor_2_node), .Q(Dout16), .clk(CLK));  // open: clr
  Register #(.width(1)) register_2 (
    .D(multiplexer_2_out), .en(pull_resistor_2_node), .Q(\传输状态Out_表明当前传输数据有效 ), .clk(CLK));  // open: clr
  Pull_Resistor pull_resistor_2 (.node(pull_resistor_2_node));
  not not_1 (pull_resistor_2_node, \使能端_低电平有效_stall_高电平有效 );
endmodule

// 组合逻辑
module \组合逻辑  (
  input  [15:0] in_1,
  output [15:0] out_2
);


  assign out_2 = in_1;
endmodule

// 字库
module \字库  (
  input  [6:0] \区号 ,
  input  [6:0] \位号 ,
  output [31:0] out_3,
  output [31:0] out_4,
  output [31:0] out_5,
  output [31:0] out_6,
  output [31:0] out_7,
  output [31:0] out_8,
  output [31:0] out_9,
  output [31:0] out_10,
  output [31:0] out_11,
  output [31:0] out_12,
  output [31:0] out_13,
  output [31:0] out_14,
  output [31:0] out_15,
  output [31:0] out_16,
  output [31:0] out_17,
  output [31:0] out_18,
  output [31:0] out_19,
  output [31:0] out_20,
  output [31:0] out_21,
  output [31:0] out_22,
  output [31:0] out_23,
  output [31:0] out_24,
  output [31:0] out_25,
  output [31:0] out_26,
  output [31:0] out_27,
  output [31:0] out_28,
  output [31:0] out_29,
  output [31:0] out_30,
  output [31:0] out_31,
  output [31:0] out_32,
  output [31:0] out_33,
  output [31:0] out_34
);

  wire [6:0] multiplier_1_cout, multiplier_1_out, subtractor_1_out;
  wire [13:0] adder_1_out, bit_extender_1_out, subtractor_2_out;

  ROM #(.addrWidth(14), .dataWidth(32)) rom_1 (.addr(subtractor_2_out), .data(out_3));  // open: sel
  ROM #(.addrWidth(14), .dataWidth(32)) rom_2 (.addr(subtractor_2_out), .data(out_4));  // open: sel
  ROM #(.addrWidth(14), .dataWidth(32)) rom_3 (.addr(subtractor_2_out), .data(out_5));  // open: sel
  ROM #(.addrWidth(14), .dataWidth(32)) rom_4 (.addr(subtractor_2_out), .data(out_6));  // open: sel
  ROM #(.addrWidth(14), .dataWidth(32)) rom_5 (.addr(subtractor_2_out), .data(out_7));  // open: sel
  ROM #(.addrWidth(14), .dataWidth(32)) rom_6 (.addr(subtractor_2_out), .data(out_8));  // open: sel
  ROM #(.addrWidth(14), .dataWidth(32)) rom_7 (.addr(subtractor_2_out), .data(out_9));  // open: sel
  ROM #(.addrWidth(14), .dataWidth(32)) rom_8 (.addr(subtractor_2_out), .data(out_10));  // open: sel
  Subtractor #(.width(7)) subtractor_1 (.a(\区号 ), .b(7'b0000001), .out(subtractor_1_out));  // open: bin, bout
  Multiplier #(.width(7)) multiplier_1 (
    .a(subtractor_1_out), .b(7'b1011110), .out(multiplier_1_out), .cout(multiplier_1_cout));  // open: cin
  ROM #(.addrWidth(14), .dataWidth(32)) rom_9 (.addr(subtractor_2_out), .data(out_11));  // open: sel
  ROM #(.addrWidth(14), .dataWidth(32)) rom_10 (.addr(subtractor_2_out), .data(out_12));  // open: sel
  ROM #(.addrWidth(14), .dataWidth(32)) rom_11 (.addr(subtractor_2_out), .data(out_13));  // open: sel
  ROM #(.addrWidth(14), .dataWidth(32)) rom_12 (.addr(subtractor_2_out), .data(out_14));  // open: sel
  ROM #(.addrWidth(14), .dataWidth(32)) rom_13 (.addr(subtractor_2_out), .data(out_15));  // open: sel
  ROM #(.addrWidth(14), .dataWidth(32)) rom_14 (.addr(subtractor_2_out), .data(out_16));  // open: sel
  ROM #(.addrWidth(14), .dataWidth(32)) rom_15 (.addr(subtractor_2_out), .data(out_17));  // open: sel
  ROM #(.addrWidth(14), .dataWidth(32)) rom_16 (.addr(subtractor_2_out), .data(out_18));  // open: sel
  assign bit_extender_1_out = {{7{1'b0}}, \位号 };  // Bit_Extender bit_extender_1
  Adder #(.width(14)) adder_1 (
    .a({multiplier_1_cout, multiplier_1_out}), .b(bit_extender_1_out), .out(adder_1_out));  // open: cin, cout
  ROM #(.addrWidth(14), .dataWidth(32)) rom_17 (.addr(subtractor_2_out), .data(out_19));  // open: sel
  ROM #(.addrWidth(14), .dataWidth(32)) rom_18 (.addr(subtractor_2_out), .data(out_20));  // open: sel
  ROM #(.addrWidth(14), .dataWidth(32)) rom_19 (.addr(subtractor_2_out), .data(out_21));  // open: sel
  ROM #(.addrWidth(14), .dataWidth(32)) rom_20 (.addr(subtractor_2_out), .data(out_22));  // open: sel
  ROM #(.addrWidth(14), .dataWidth(32)) rom_21 (.addr(subtractor_2_out), .data(out_23));  // open: sel
  ROM #(.addrWidth(14), .dataWidth(32)) rom_22 (.addr(subtractor_2_out), .data(out_24));  // open: sel
  ROM #(.addrWidth(14), .dataWidth(32)) rom_23 (.addr(subtractor_2_out), .data(out_25));  // open: sel
  ROM #(.addrWidth(14), .dataWidth(32)) rom_24 (.addr(subtractor_2_out), .data(out_26));  // open: sel
  Subtractor #(.width(14)) subtractor_2 (.a(adder_1_out), .b(14'h1), .out(subtractor_2_out));  // open: bin, bout
  ROM #(.addrWidth(14), .dataWidth(32)) rom_25 (.addr(subtractor_2_out), .data(out_27));  // open: sel
  ROM #(.addrWidth(14), .dataWidth(32)) rom_26 (.addr(subtractor_2_out), .data(out_28));  // open: sel
  ROM #(.addrWidth(14), .dataWidth(32)) rom_27 (.addr(subtractor_2_out), .data(out_29));  // open: sel
  ROM #(.addrWidth(14), .dataWidth(32)) rom_28 (.addr(subtractor_2_out), .data(out_30));  // open: sel
  ROM #(.addrWidth(14), .dataWidth(32)) rom_29 (.addr(subtractor_2_out), .data(out_31));  // open: sel
  ROM #(.addrWidth(14), .dataWidth(32)) rom_30 (.addr(subtractor_2_out), .data(out_32));  // open: sel
  ROM #(.addrWidth(14), .dataWidth(32)) rom_31 (.addr(subtractor_2_out), .data(out_33));  // open: sel
  ROM #(.addrWidth(14), .dataWidth(32)) rom_32 (.addr(subtractor_2_out), .data(out_34));  // open: sel
  DotMatrix #(.inputtype("row"), .matrixcols(32), .matrixrows(32), .dotshape("circle")) dotmatrix_1 (
    .row0(out_3), .row1(out_4), .row2(out_5), .row3(out_6), .row4(out_7), .row5(out_8), .row6(out_9),
    .row7(out_10), .row8(out_11), .row9(out_12), .row10(out_13), .row11(out_14), .row12(out_15),
    .row13(out_16), .row14(out_17), .row15(out_18), .row16(out_19), .row17(out_20), .row18(out_21),
    .row19(out_22), .row20(out_23), .row21(out_24), .row22(out_25), .row23(out_26), .row24(out_27),
    .row25(out_28), .row26(out_29), .row27(out_30), .row28(out_31), .row29(out_32), .row30(out_33),
    .row31(out_34));

  // Other names for the same wires on the sheet: D0[31:0] = out_3; D1[31:0] = out_4; D2[31:0] = out_5;
  //   D3[31:0] = out_6; D4[31:0] = out_7; D5[31:0] = out_8; D6[31:0] = out_9; D7[31:0] = out_10; D8[31:0] = out_11;
  //   D9[31:0] = out_12; D10[31:0] = out_13; D11[31:0] = out_14; D12[31:0] = out_15; D13[31:0] = out_16;
  //   D14[31:0] = out_17; D15[31:0] = out_18; D16[31:0] = out_19; D17[31:0] = out_20; D18[31:0] = out_21;
  //   D19[31:0] = out_22; D20[31:0] = out_23; D21[31:0] = out_24; D22[31:0] = out_25; D23[31:0] = out_26;
  //   D24[31:0] = out_27; D25[31:0] = out_28; D26[31:0] = out_29; D27[31:0] = out_30; D28[31:0] = out_31;
  //   D29[31:0] = out_32; D30[31:0] = out_33; D31[31:0] = out_34

  // Notes on the sheet:
  //   contents of rom_1 (hex, n*v repeats v):
  //   281*0 ffffffff 272*0 60000000 202*0 18000 3c000 0 0 18000 3c000 0 0 18000 3c000 8*0 18000 18000
  //   3c000 3c000 18000 18000 3c000 3c000 18000 18000 3c000 18000 3c000 3c000 18000 3c000 18000 18000
  //   3c000 18000 3c000 3c000 18000 3c000 8*0 4*18000 4*3c000 4*18000 3c000 18000 3c000 3c000 3c000 18000
  //   18000 3c000 18000 3c000 3c000 3c000
  //   contents of rom_2 (hex, n*v repeats v):
  //   150*0 1c000 9*18000 121*0 ffffffff 269*0 10000 0 60000000 60000000 202*0 3c000 3c000 0 0 3c000 3c000
  //   0 0 3c000 3c000 8*0 24*3c000 8*0 24*3c000 587*0 8000 11*0 2000 124*0 8000 28*0 8000 291*0 400000
  //   742*0 1000 189*0 80 822*0 10000 654*0 40000 50*0 20000 64*0 4000 252*0 20000 56*0 40000 51*0 2000
  //   74*0 1000000 18*0 8000 74*0 2000 8*0 800000 400*0 40000 676*0 20 393*0 20000 31*0 2000 547*0 100
  //   58*0 800000 200 1000000 200200 387*0 1000000 5*0 800000 26*0 800000 22*0 8000 22*0 10000 0 8000 10*0
  //   10000 241*0 800000 0 0 1000000 7*0 1000000 1000000 10*0 1000000 9*0 20000 41*0 1000 301*0 20000 18*0
  //   800000 800000
  //   contents of rom_3 (hex, n*v repeats v):
  //   150*0 1ffc00 9*3ffc00 59*0 ff000 26*0 7ff0 0 ffe0000 30*0 10000 109*0 1c0000 144*0 60000006 0
  //   60000006 13*0 40000002 38000 0 60000000 e0000000 15*0 181800 0 0 0 e6000 182*0 3c000 3c000 0 0 3c000
  //   3c000 0 0 3c000 3c000 8*0 24*3c000 8*0 24*3c000 581*0 1800 1801800 8100 3000 60000 c00 c000 383800
  //   7000020 181800 0 e0 0 c200c00 1800000 30000 c06000 1003000 3000 1c000 1000 70000 2000 0 18000 0
  //   600c00 e00800 e00000 3000020 1040300 60000 6007000 6000 181800 3000018 1800000 0 0 3801800 0 8000 0
  //   3006000 2000 6100000 1800000 1800000 3000000 80 0 100800 20000 1800c00 0 3000000 800000 1800 80000
  //   301800 0 8000 30000 1800020 c00000 8 3800040 e00020 1000400 1801800 603000 c000100 30000 60000 1c00
  //   700000 300000 3818000 3803800 1800 18000 3803800 1800 1000c00 6003800 c06000 3000 181000 4000 200000
  //   30000 10 181c00 80 e00000 0 300c000 60000 3006000 1000000 100 181800 3001800 6040020 c00000 1c00
  //   1c3800 60000 102000 c3000 182000 0 2000000 602000 0 180000 c0000 2002000 6000c00 30000 380c00 18000
  //   1003000 1c000 0 8 0 c00 40180 0 70000 4000 0 1801000 1001c00 600 383000 381800 600c000 6004000
  //   c00c000 c0 18000 e000 1800000 400600 600c00 0 1800 c00 c00 200 400 c606000 3000 3000 30 18000 800000
  //   70000 40000 600c200 6000300 4018200 3000 3800000 300000 0 30000 c00800 400800 20 e000 180c000 200
  //   70000 3000 30000 3001000 0 2000 3000000 0 380 60000c0 2000000 c000 400400 c00 101000 10000c0 1001800
  //   3001800 1c00 4003300 e00e00 3801b80 3000c00 1800c00 c03000 30000 c00600 c00 1900 30100 0 0 3001000
  //   60000 3000 1000800 1c00 0 30000 1c000 3803000 c00000 2000000 3003000 1c00 603800 1c001c0 3000 1c0 20
  //   0 1e0 1c000 183000 1c1c00 300000 20000 c0 3000 6020000 6006000 1000c00 301800 800800 18000 6000
  //   183000 2000000 3000300 3806300 c3000 181800 0 c01800 1800000 0 0 0 c0 3000000 0 101800 301c00 1c000
  //   1800 1018300 38000 6000 800400 2000 3000020 202000 100180 380c000 3803000 30080c0 2004000 8000 1800
  //   3001800 30000 6000000 c00000 100 0 3000000 18000 18200 800000 1803000 0 0 600700 1800000 0 400000
  //   c00000 1800800 2000600 600000 30000 40000 60c080 1c00 3000800 60000 1000800 2020080 1380030 1040000
  //   40100 2010000 0 0 18000 1000080 6001800 0 3000 c00c00 2000180 3000c00 3000 600 3000000 8000 0 380
  //   100000 400000 0 c00 0 0 c00 100000 6000 c000 3001800 0 8000000 0 0 c00 300 1c000 403000 0 1c000
  //   3000000 180 3800000 60000 1800 18000 1c000 70000 3000800 10 1c00 c00 100000 1c00 1c00c00 0 800000 0
  //   0 60000 3000000 10000 7000000 10 c180 180 3000400 8000400 1800 600e00 400 800 18000 3006000 1800200
  //   0 3800c00 0 30000 3006000 601000 c00000 1800 18000 c000 38000 2003000 18000 0 400000 6000 1002000
  //   3000000 2000040 100 70000 3807000 800 0 6000 1800 70000 600 1800 c000 101000 c0 3200 1800 200c00
  //   18000 0 3800 300010 0 c000 80 181800 30000 200000 401000 201800 4000 1c00000 30c0 1c00800 c00000
  //   1800 1801800 30000 1000800 18000 c01c00 6000 c000 1803000 6000 60 1c001c0 70000 1800 8080 2000000
  //   1000080 300c300 3001000 200e100 1008100 4003000 1801800 6000 800000 38000 0 0 806000 300c00 418400
  //   c00 600000 e1ee00 408000 c03800 3000 30000 1800 1000000 800100 600c00 60000 3810180 0 0 1800000 0
  //   2020180 0 0 10180 20 10000 1000800 18000 181800 3801800 0 3003000 30 1800000 e0000 3000c00 100 10
  //   100010 2001800 8060180 c000 1001800 400000 c01800 0 1000000 0 1800c00 0 4100 0 2000000 c00000 e000
  //   1000 1800 800800 1000 8000 20020 3003000 1000000 30000 1800 381c00 1801800 30000 400c00 20100 3000
  //   e00000 1001000 1000 6600 38000 c6000 1800800 c03000 30000 400000 600000 18000 6001800 300c00 6000 0
  //   0 0 100 0 0 3001800 0 1000 0 c00 181800 1880 3001840 1000 3180 200 0 0 0 2000000 8 200 3001800 20000
  //   0 100 30000 80000 183800 300c700 800 3801000 1800000 6000000 2000 8000000 10000 1800100 1000 1c00 0
  //   0 c000 600000 600000 38000 1801c00 800 3000 3000 3000 1800 1800000 3001800 800 18000 2000 1800800
  //   c00 3000000 6002000 40000 300000 1000000 2000c00 400c00 1000 0 20300c0 1000 8080 c00e00 1800008 0
  //   3000c00 180 c0 3000000 1000 18000 30000 2000000 e00000 0 0 c00 0 3007000 3000 600 200 200600 1800c00
  //   1800008 8600 3000700 0 0 1000000 0 0 6000200 4*0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
  //   contents of rom_4 (hex, n*v repeats v):
  //   11*0 c3000 5*0 40 2000000 10 8000000 80 0 1ff0 100000 1ff0 f80000 1fff0 fff8000 1ffe0 7ff0000 18*0
  //   800 3800 13*0 10000 18000 0 c00000 c20000 0 18000 0 0 0 400 3e000 0 10000 10000 13*0 18000 57*0
  //   10*f00f00 34*0 c00000 24*0 3ffe00 26*0 7ff0 1800000 ffe0000 0 0 300 26*0 1c0 18000 3c00000 49*0 1c0
  //   57*0 80000 1e0380 0 0 0 180 11*0 70 11*0 20000 0 0 18000 0 0 80 0 0 0 3c0 0 0 1e0 5*0 c0 18*0 6000 0
  //   0 0 e0000 74*0 3800001c 0 7000000e 13*0 60000006 38000 0 60000000 e0000000 15*0 1c1c00 0 0 0 e7000
  //   104*0 200000 18180000 6000000 13*0 60000 0 0 300000 0 0 6000 6*0 30000 3000 0 0 0 20000 0 300 0
  //   38000 3000 0 0 30000 0 0 2000000 60000 31*0 3c000 3c000 0 0 3c000 3c000 0 0 3c000 3c000 8*0 24*3c000
  //   8*0 24*3c000 579*0 218008 30600008 3801c00 1c01c00 e380 3800 38000 1800e00 6000 383010 78001f0
  //   1c1c00 18030 1ff0 2301c0 e380600 3c00000 18000 e07000 3c01800 1800 301e000 1800 38000 8103000
  //   3ffff80 1c000 0 700e00 e00e00 e00000 18000f0 1ce0700 70000 7007000 800e000 1c1c00 380001c 1c00700
  //   600 0 3803c00 2000 e000 0 3807200 3800 7180000 1c00000 1c00000 3800000 3ffffc0 6000060 380f00 38000
  //   1c00e00 10 3840010 1e00000 83c00 3c0000 f83800 60000 e000 3038000 1c000e0 c04080 41fffc 38001e0
  //   e00070 1c00600 1c01c00 703800 6000180 38000 70000 1801c00 601008 300010 3818000 3801c00 8200c00
  //   3018000 3803800 e00 1c00e00 7001c00 e03800 8003800 1c3800 7000 780000 18000 1001c 1c1c00 3ffffc0
  //   e40040 e40080 780f000 38000 380f000 1c30060 1ffff80 3c3800 3801c00 70ffff0 e00000 1c00 1c3800 70000
  //   3c3800 c3810 1c3800 800080 3800000 f03000 180000 1c0000 1e0200 3803800 3000c00 38000 380e00 1c000
  //   3c03800 381c060 1800008 18 18 10230c30 c0301c0 8000030 60200 6007000 c018808 1c01c00 1801c00 600
  //   383800 381c00 700e000 700e000 e00e000 fe0 c000 7000 1c00000 700700 8710e00 c0000 e00 e00 8040600
  //   8000380 10270700 e706000 6003800 1801c00 800f0 1c000 e00008 38000 70000 300e380 3000380 701c380
  //   c003800 3800000 380000 8 38000 8e60c00 8720c00 4010038 7000 1c0e000 4000380 18060008 c001800 18000
  //   3801c00 700 10003800 3800000 10 1f80 70180e0 3800000 e000 300e00 c00 1c1c00 18007e0 1c01c00 7801c00
  //   c001c00 70039c0 e00e00 3801dc0 3800e00 1c01e00 f03c00 30000 e00700 8000e00 c201cc0 18030180 4001c00
  //   180070 3801d00 70000 3b00 1801c00 3801c00 18 38000 1c000 3803800 600000 7807000 3801800 301c00
  //   703c00 1e001e0 3800 100c01c0 1f0 f0 7ff0 fe030 183800 181c00 380000 70000 7ffffe0 3800 7070008
  //   7007000 1c00e00 381c00 e01e00 3c000 c007000 1c3000 7020100 3000380 3007380 c3800 1c1c00 4000008
  //   e01c00 1c00018 2040040 c202038 6000060 c0e0 38000e0 80 381c00 381c00 1c000 1c00 381c380 1c000 c2000
  //   600f00 8003800 38000e0 303800 3801c0 380e000 3807000 38060e0 700e000 601c000 1000c00 3800e00 38000
  //   3000000 e00018 ffff80 180000 3800180 1c100 c18300 e00300 1e03800 c1000c0 18 700700 1c00040 20020
  //   700000 e00000 1c00e00 3800700 700000 30400 18060000 70e1c0 1e00 3800e00 f0000 1c00e00 30301c0
  //   1b80038 3870000 8060180 3018000 4000030 20 1c000 1ffffc0 7001c00 c000000 10203800 e00e00 18001c0
  //   3800e00 383800 3800680 3004840 e600 1800100 7fc0 790010 e00020 c004840 6000ec0 300 c0600c0 e00
  //   380000 7000 e000 3801c00 6061000 e003800 4000000 1c00 e00 380 1c000 603800 0 1c000 3800000 7c0
  //   3c00000 30000 1c00 1c000 301c060 38000 3800e00 301c 1e00 18180e00 7a0008 381e00 1c01e00 71c000
  //   1e00008 6180 0 70000 1c00000 1c000 7000000 6000038 e180 60001c0 7806700 c000700 10203800 700e00 700
  //   1c01c00 38030 3803800 1c00380 c00c00 3c00e00 1c00070 1c000 3806000 701c00 e06040 1c00 18000 e000
  //   1c000 3801800 1c000 1800000 f00018 7800 1c07800 38000e0 38001e0 1f80 78000 3007800 e00 30 8007000
  //   3801c00 70040 c0c700 3801c00 6000 1c1c00 80e0 3303b00 180c00 380e00 c01c000 c000010 383c00 300038
  //   10118030 1800f000 880e0 1c1c00 38000 380000 701c00 701c00 f000 1c00000 38c0 1c01c00 e00040 10300c00
  //   1c03c00 18000 3800e00 301c040 1ec1c00 7000 e000 1c01800 3000 ffe7ff0 1e001c0 78000 1c00 c1c0 383ffe0
  //   38081c0 380e380 3801c00 380e380 381c380 6003800 1c01c00 7000 1c00000 38000 1ffff80 10 e07000 380e80
  //   71c700 e00 706000 f0c780 e0ee00 1e03800 c003800 78000 41c00 1c00000 ffff00 300e00 3070000 381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
  //   contents of rom_5 (hex, n*v repeats v):
  //   8*0 40000 0 0 c3000 0 20 3c00000 1820 3c70000 e0 6000000 30 18000000 198 19800000 1800 100000 1830
  //   d80000 1ffe0 7ff8000 1ffc0 7ff0000 18000 0 0 0 18000 12*0 7e000 3c00 7c00 6*0 30000 c000 10 4000000
  //   0 0 0 18000 ff000 800000 1c00000 1c70000 2000000 18000 18000018 0 c000 7000c00 ff800 0 18000 18000
  //   3c000 7e000 7e000 18000 18000 0 0 18000 18000 0 0 0 18000 18000 3ffffff8 18000 301c00 4008060
  //   3000000 0 180 820 8000 2000000 7*0 4000 1c000 c000 0 c0e00 0 0 8000 0 1000 0 1000 0 0 10300 0 1ff00
  //   3000 0 1c01000 7*1000080 1000180 12*1000080 1c00180 9*1c00380 0 0 10*1000080 0 0 1ff800 1fe7fc0
  //   7fdffbfe 1fffc0fc 7f81fe0 7fc1fffc 7f07fffe 7e0ffffe 3fffc1fc 7fc1fc0 1fe0fffc 7f83fffe 7*0 1f8000
  //   1c00000 20 4000000 5*0 c00 16*0 f80700 26*0 7000 c00000 e0000 18000 0 700 9*0 38000 16*0 780 18000
  //   e00000 0 30000 70000 0 0 0 80000 18*0 1c000 30000 0 0 0 e000 0 0 c0000 180000 0 0 180 0 0 0 80000 0
  //   0 0 300000 0 0 180 260 12*0 30000 19*0 10000 14*0 c000 3000 0 20000 4*0 c000 0 e0000 e0980 70000
  //   601c0 40000 1800c0 0 c0 7000 6040 0 0 0 180 0 300 600 38 38000 100 7000 6000 0 e0400 30 c00 30 e0000
  //   0 38000 0 0 1e000 2000 0 60 0 300000 0 240 0 60 120 0 100 200 18000 40180 1e0 0 f0000 30000 3000 c00
  //   0 780000 6*0 18000 0 0 0 c00 7000 0 c00 3c0000 700c0 18000 e0000 41*0 10000 0 7f000 28*0 1e000078 0
  //   3000000c 13*0 3000000c 38000 0 60000000 60000000 15*0 181c00 0 0 0 7e000 104*0 600000 c300000
  //   7000000 12*0 300000 70000 0 0 380000 60000 3000 7000 100400 0 0 3800 10000 0 38000 3000 400 0 200
  //   38000 18000 300 0 1c000 c03c00 7f0 0 38000 0 7c00 3800000 78000 60000 c000 70000 300 27*0 3c000
  //   3c000 0 0 3c000 3c000 0 0 3c000 3c000 8*0 24*3c000 8*0 24*3c000 579*0 3ffffc 3ff3fffc 3803800
  //   1803800 c380 7000 1c000 3800c00 7010 383038 7003ff0 181c00 dfff8 7ffff0 1ff181c0 c300700 3800020
  //   1c000 c0e000 3801c00 1c00 381c070 1fe00c00 18000 ff81c00 3ffffc0 18000 10 600e00 e10c00 c00000
  //   1c007f0 38e0700 40000 7006000 600c000 181800 38c1018 1c08600 8600 60 3023810 103000 6000 0 3806380
  //   8183300 6184010 1800010 1818030 383fff0 18000 7fffff0 7003c0 78000 1800c00 1ffffff8 387fff8 1c00018
  //   1ffc3800 1fc0018 7f83000 330018 30c008 3030420 18003f0 1807fc0 221fffc 3800ff0 18c003f0 1804600
  //   1801800 e03000 70030c0 38000 60000 1c01c20 601ffc 309ff8 3018618 3000c00 1ff00e08 3818010 3803000
  //   100e10 1800c00 7000c00 1c01800 6001c10 1c3800 c10e000 700000 1c018 fff8018 181c08 3ffffc0 c7ffe0
  //   e7ffc0 700e000 38000 300e000 183fff0 1c00180 703800 3003800 70e0060 c00018 181800 1c3000 c0000
  //   383800 c3ff8 1c3070 ffffc0 383fff0 e01800 101d0018 380200 1fff00 3801800 3800c00 30000 380c00 18000
  //   3803800 381c070 38ff7fc 1ffffffc 3ffffffc 1ff30c38 7018380 c1ffff8 ffff00 7007000 fffcffc 3803808
  //   3c01800 60c00 383818 381808 700e000 600e060 e00e060 1ffe0 e000 3008 e00030 10620e00 e638c00 60300
  //   c040600 c040600 ffe0610 e10c180 1ff60600 c60e008 3003000 3800c00 1ffc0ff8 c000 1e0001c 1c008 38000
  //   380c180 3860180 3018180 6001800 3800070 304030 1feffffc 38000 ee71c00 c671c00 7ff8038 3008 180c030
  //   6000340 c06001c 6081800 1c000 3000c00 7f80 18003000 3000018 3ffffff8 fffc0 700c0c0 380001c 7000
  //   380e00 c00 181800 180ffe0 1831d80 7001800 7001800 60038c0 e00e00 38018e0 3800c00 3801c00 e03800
  //   60000 c00600 ff00c00 ff01ce0 c030180 7001c00 1ffc00f0 30019c0 70000 31c0 c01c00 3801800 3ffffffc
  //   78000 1c000 7027010 700808 7007000 3001c00 30781808 703900 1c001c0 3000 1ffe01c0 10203ff8 1ff01ff0
  //   3ffffc0 3ffc038 183808 181c38 3f8030 f0000 7ffffe0 c3900 607001c 700e000 1800e00 381c00 1c01c00
  //   78000 6007000 183018 703ff80 30c1380 3006300 c3000 181810 7fffffc 1c01800 3a00018 3fc7fc0 63ff038
  //   7fffff0 183060c0 3000ff0 7ffffc0 381800 301c08 18000 301c00 3818300 400c008 1e3000 300e00 6001800
  //   38007f0 303020 f001c0 381c100 380e000 30070c0 700e100 301c200 3c00600 7000600 1c000 187fff0 617ffc
  //   ffff80 303b0030 387ffc0 1818380 e18700 e00780 1c03860 ffbffe0 3fffffc 8718700 181ffe0 3fff0 720060
  //   c0fff8 1800c00 3800600 601818 307f8 1c060ff8 c18380 1c00 3800c00 e0000 1800e00 30181c0 3b88630
  //   3c60000 6030380 3018408 ffffff8 3000030 18000 18001c0 7001c00 6040008 1ff07000 c01c00 1c0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
  //   contents of rom_6 (hex, n*v repeats v):
  //   4*0 1ff800 300c00 181800 0 70000 0 0 c3000 0 c0 3c00000 20c0 3cf8000 1c0 3000000 30 c000000 1b0
  //   18c00000 1800 100000 1bf0 d80000 180c0 3018000 1ffc0 3ff0000 18000 0 0 0 18000 c000030 7ffff80
  //   1ffffff8 4*0 180 18000 8060 0 0 3ffc00 6e00 ce00 5*0 300 30000 c000 70 7800000 0 0 0 18000 1e7800
  //   7e00000 1c00000 1c70000 f80fc00 ff000 c1ff830 800 7f800 1f801800 c3800 0 18000 18000 3ffc00 3ffc00
  //   3ffc00 3c000 3c000 ffffff0 ffffff0 18000 18000 c018030 0 0 18000 18000 3ffffffc 3c000 781c00 e03c0f0
  //   7800000 0 1c0 1c70 1ce38 f000000 7*0 1c000 7f800 7f800 1800 1ffe00 1f800 1fff00 7f000 7f000 c07c00
  //   c01800 c0fe00 c0fc00 c00300 1c1ff00 c07e00 c1ff00 c0fc00 c0fc00 7f07c00 30080c0 301c0c0 30180c0
  //   30000c0 30c38c0 301c0c0 31ff8c0 30180c0 301c0c0 31000c0 31004c0 3103ec0 3183cc0 31806c0 3187ec0
  //   3181ec0 310ffc0 3183cc0 3183cc0 33c1cc0 10*30000c0 0 0 10*30000c0 0 0 ff000 1fe3f80 7fcff3f8 fcf0078
  //   7f00fe0 3f81fffc 3f03def8 7c0ffbfc 1fcfc0f8 3fc0fc0 1fc07bf8 3f01cffc 5*0 ff807f0 1e00030 39e000
  //   1c00000 c0 3000000 0 18000 0 0 0 c00 5*0 180400 0 0 18000 6*0 1f80000 1e001c0 0 1ffe000 1e100
  //   1ff8000 1ffff00 1ffff00 7c000 3f81fc0 ff000 ff800 3fc3f80 1fe0000 f0000f0 7800fe0 38000 1fff000
  //   18000 1fff000 78000 ffff00 0 3f80fc0 f87e1f0 1fc1fc0 3f80fc0 7fff00 7000 e00000 e0000 3c000 0 380 0
  //   180000 0 1800 0 fc00 0 180000 18000 3c000 7c0000 78000 14*0 600 18000 700000 0 30000 70000 0 0 0
  //   60000 0 e0000 0 300000 0 1c0 80000 380 c000 30000 c03800 e1c0 0 100 3c0000 380000 380000 300000 e000
  //   38080 6000 7000 f000 3f000 e0000 c0000 e0000 c0000 0 0 c0 0 0 e0000 e0000 c0000 800000 60000 380000
  //   0 0 e0 260 0 c0 1c0 0 180 80700 0 0 0 600 0 19c0 38000 38000 300000 1c000 18000 0 0 0 8000 0 20000
  //   80000 300000 6000 1c0000 3000 0 80000 0 4000 30000 c0000 13*0 7000 3800 38000 38000 0 0 c000 c000
  //   e000 c0 e0000 e0e80 70000 700c0 60000 1c0640 0 60 303800 207270 f0000 0 1000 c0 70000 180 700 1d8
  //   38000 601c0 7800 f070 60800 70700 198 1fe00 7c18 f0000 401c0 38000 3800 1800 e000 3800 0 230 1c0
  //   1c0000 300 640 1c00 330 320 0 1c0 780 1e000 78cc0 78320 0 3e000 38000 1c00 1fe00 380000 380000 0 0
  //   3000 1800 fc00 7800 e000 380000 0 0 807e00 7000 0 dffe00 1e0000 70760 1e000 70000 22*0 18000 4*0
  //   101e00 7e000 0 0 3c000 9*0 fe000 0 e3800 0 7e000 0 3e000 0 0 3c0000 0 0 1fe000 6*0 1c000 11*0
  //   7c001e0 0 38000018 13*0 1ffc7ffc 38000 0 60000000 60000000 10*0 fffe00 1ffe000 f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
  //   contents of rom_7 (hex, n*v repeats v):
  //   4*0 3ffc00 1c3800 3c3c00 0 60000 0 0 c3000 0 180 3c00000 6180 3cf8000 180 1800000 60 c000000 330
  //   cc00000 1800 100000 1be0 d80000 18180 1818000 1ff80 1ff0000 18000 80 38000 18000 3c000 c000030
  //   3ffff80 ffffff0 0 3c000 0 1800180 180 18000 c060 18 0 780e00 ce00 cc00 5*0 300 30000 c000 3e0
  //   3e00000 0 1c00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
  //   contents of rom_8 (hex, n*v repeats v):
  //   5*0 77000 3c3c00 0 60000 0 0 c3000 0 180 3c00000 c180 3c78000 300 c00000 60 6000000 320 c600000 1800
  //   100000 1a00 d80000 18180 1c18000 1ff00 ff0000 18000 30001c0 7c000 3c000 3c000 6000060 3800380
  //   1c00380 1800180 1ff800 0 3c003c0 180 18000 180c0 70 0 1c00300 c000 c000 5*0 600 30000 c000 1f00
  //   7c0000 0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
  //   contents of rom_9 (hex, n*v repeats v):
  //   5*0 3c000 181800 0 c0000 0 0 c3000 0 300 c00000 1c300 c30000 600 600000 c0 6000000 660 6600000 1800
  //   100000 1a00 d80000 18300 c18000 1ff00 ff0000 18000 1800380 7c000 7e000 66000 6000060 1c00080 1c00380
  //   1800180 7ffe00 3fffc0 3e007c0 300 18000 380c0 e0 7e000 3800180 c000 c000 0 1800f80 0 0 0 c00 30038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
  //   contents of rom_10 (hex, n*v repeats v):
  //   5*0 18000 0 0 c0300 0 0 c3000 0 3c0 1800000 1e3c0 1830000 400 600000 c0 3000000 660 6300000 1800
  //   100000 1a00 d80000 18600 618000 1fe00 7f0000 18000 c00700 7c000 3c000 66000 30000c0 e000c0 1c00380
  //   1800180 e00700 7fffc0 3e007c0 300 18000 30180 1c0 3ffc00 30000c0 18000 1c000 0 7803fe0 0 0 0 c00
  //   301f0 f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
  //   contents of rom_11 (hex, n*v repeats v):
  //   8*0 187f80 0 0 c3000 0 7c0 1000000 1f7c0 1060000 400 600000 180 3000000 cc0 3300000 1800 100000 1a00
  //   d80000 18600 618000 1fc00 7f0000 18000 600e00 38000 3c000 63000 30000c0 e00040 1c00380 1800180
  //   c00300 e00000 3c003c0 300 18000 60180 380 f00f00 6000060 18000 1c000 ffffff0 e007070 f00000 0 0 1800
  //   30f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
  //   contents of rom_12 (hex, n*v repeats v):
  //   7*0 31c00 1ff700 0 0 c3000 0 3c0 2000000 1f3c0 20c0000 400 600000 180 1800000 cc0 3180000 1800
  //   100000 1a00 d80000 18c00 318000 1fc00 3f0000 18000 301c00 0 0 c3000 1800180 700000 1c00380 1800180
  //   1c00380 1800000 800100 600 18000 60300 700 1c00380 e000060 18000 1c000 1ffffff8 c00c030 3fc0000
  //   800700 f00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
  //   contents of rom_13 (hex, n*v repeats v):
  //   7*0 71c00 360600 0 0 c3000 0 3c0 4000000 1e3c0 4180000 400 600000 300 1800000 1980 1980000 1800
  //   100000 1a00 d80000 18c00 318000 1fc00 3f0000 18000 183800 0 0 c1800 1800180 780000 1c00380 1800180
  //   1800180 3800000 0 600 18000 c0300 e00 38001c0 c000030 18000 7f000 0 1c018038 70f0018 7803fc0 3fc07f0
  //   1fff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
  //   contents of rom_14 (hex, n*v repeats v):
  //   0 0 0 3c000 0 0 0 73800 200600 0 1e00000 c3000 0 80 0 4080 0 400 600000 300 c00000 1980 18c0000 1800
  //   100000 1a00 d80000 18800 318000 1f800 3f0000 18000 c7000 0 0 181800 c00300 380000 1c00380 1800180
  //   1800180 3000000 0 600 18000 c0600 1c00 60000e0 c000030 18000 fb800 0 1c030038 c03c030 e0070e0
  //   70f1e00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
  //   contents of rom_15 (hex, n*v repeats v):
  //   0 0 0 7e000 0 0 0 63800 400c00 0 7f80008 c3000 e03c070 4*0 400 600000 600 c00000 3300 cc0000 1800
  //   100000 1a00 d80000 19800 118000 1f800 3f0000 7ffffe0 6e000 0 0 181800 c00300 1c0000 1c00380 1800180
  //   1800180 3000000 0 c00 18000 180600 3800 e000070 1c038030 18000 198c00 0 c070030 1800f0e0 c00c030
  //   c03b0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
  //   contents of rom_16 (hex, n*v repeats v):
  //   0 0 0 ff000 0 0 0 e3000 800c00 0 e1f0018 c3000 1f07c0f8 4*0 400 600000 600 600000 3300 c60000 1800
  //   100000 1a00 d80000 19800 198000 1f800 3f0000 7ffffe0 3c000 0 0 300c00 600600 1e0000 1c00380 1800180
  //   1800180 3ffff80 0 c00 18000 180c00 6000 c000030 1807c030 18000 198c00 0 e0e0070 3fc0 1801c030
  //   1801e00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
  //   contents of rom_17 (hex, n*v repeats v):
  //   0 0 0 ff000 0 0 0 c7000 1800 ffffffff 1803e030 c3000 1f07e1f8 4*0 400 600000 c00 600000 6600 460000
  //   1800 100000 1a00 d80000 19800 198000 1f800 3f0000 18000 38000 ffffff0 0 300c00 600600 e0000 1c00380
  //   1800180 1800180 3ffffc0 0 c00 18000 301c00 c000 18000018 1807e038 18000 198c00 1ffffff8 7fc01e0 f00f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
  //   contents of rom_18 (hex, n*v repeats v):
  //   0 0 0 ff000 0 0 0 c6000 1000 0 10007fe0 c3000 1f07c0f8 4*0 400 600000 600 600000 3300 c60000 1800
  //   100000 1a00 d80000 19800 198000 1f800 3f0000 18000 3c000 7ffffe0 0 600600 300c00 70000 1c00380
  //   1800180 1800180 3ffff80 0 1800 18000 301800 18000 18000018 1807c030 18000 198c00 0 1f00180 3fc0000
  //   1c030030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
  //   contents of rom_19 (hex, n*v repeats v):
  //   0 0 0 fe000 0 0 0 186000 3000 0 20000fc0 c3000 e03c0f0 4*0 400 600000 600 c00000 3300 cc0000 1800
  //   100000 1a00 d80000 19800 118000 1f800 3f0000 18000 6e000 0 0 600600 300c00 60000 1c00380 1800180
  //   1800180 3000000 0 181800 18000 603800 30000 10000008 1c03c030 18000 199c00 0 0 70f0018 c0e0070
  //   e03b800 30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
  //   contents of rom_20 (hex, n*v repeats v):
  //   0 0 0 7e000 0 0 0 18c000 42000 0 100 c3000 5*0 400 600000 300 c00000 3180 18c0000 1800 100000 1a00
  //   d80000 18800 318000 1f800 3f0000 18000 c7000 0 0 c00300 181c00 c0000 1c00380 1800180 1800180 3000000
  //   0 3c1800 18000 603000 60000 0 c000030 18000 db800 0 0 c03c030 7bc01e0 7ff1ff0 1ffffff0 3f0000 f800 1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
  //   contents of rom_21 (hex, n*v repeats v):
  //   7*0 10c000 36000 0 0 c3000 5*0 400 600000 300 1800000 1980 1980000 1800 100000 1a00 d80000 18c00
  //   318000 1fc00 3f0000 18000 183800 0 0 c00300 181800 180000 1c00380 1800180 1800180 3800000 0 6e3000
  //   18000 c06000 c0000 0 c000030 18000 7f000 0 1ffffff8 1800f0e0 3f803c0 3fc07e0 1ffffff0 7e000 7c000
  //   f8001f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
  //   contents of rom_22 (hex, n*v repeats v):
  //   0 1c000000 3c00000 4*0 308000 1c000 0 0 c3000 5*0 400 600000 180 1800000 18c0 3180000 1800 100000
  //   1a00 d80000 18c00 218000 1fc00 7f0000 18000 301c00 0 0 1800180 c3800 380000 1c00380 1800300 1800180
  //   1800000 0 73000 18000 c06000 180000 0 c000070 18000 3c000 1ffffff8 ffffff0 3fc0 0 0 c0000 3fc00
  //   3ec000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
  //   contents of rom_23 (hex, n*v repeats v):
  //   0 f000000 7e00000 4*0 200000 e000 0 0 c3000 5*0 400 600000 180 3000000 cc0 3300000 1800 100000 1a00
  //   d80000 18600 618000 1fc00 7f0000 18000 600e00 38000 38000 1800180 c3000 300000 1c00380 c00300
  //   1800180 e00000 3c003c0 73000 18000 180c000 300000 0 6000060 18000 18000 ffffff0 0 f00 0 0 180000
  //   31f80 1f0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
  //   contents of rom_24 (hex, n*v repeats v):
  //   0 3c00000 c200000 5*0 7000 0 0 c3000 5*0 400 600000 c0 3000000 c60 6300000 1800 100000 1a00 d80000
  //   18600 e18000 1fe00 7f0000 18000 c00700 7c000 7c000 1000180 67000 600040 1c00380 e00600 1800180
  //   7fff80 3c007c0 3f000 18000 180c000 600000 0 70000e0 38000 18000 5*0 300000 303f0 f80c000 fc000 3f000
  //   0 7e0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
  //   contents of rom_25 (hex, n*v repeats v):
  //   0 1e00000 c300000 5*0 7800 0 0 c3000 5*0 400 600000 c0 6000000 660 6600000 1800 100000 1a00 d80000
  //   18300 c18000 1fe00 ff0000 18000 1800380 7c000 7c000 30000c0 66000 c000c0 1c00380 7c3c00 1800180
  //   3fffc0 7e007c0 1e000 18000 3018000 c00000 0 38001c0 30000 18000 5*0 300000 30078 1e00c000 1f800
  //   f8000 0 7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
  //   contents of rom_26 (hex, n*v repeats v):
  //   0 e00000 c300000 5*0 3800 0 0 c3000 5*0 600 c00000 60 6000000 660 c600000 1800 100000 1a00 d80000
  //   18300 1818000 1ff00 1ff0000 0 30001c0 7c000 3c000 30000c0 3e000 1c00180 1c00380 1ff800 1800180 0
  //   3c007c0 e000 18000 7018000 3800000 0 1c00380 30000 30000 0 ffffff0 0 0 0 600000 30000 c000 3f00
  //   7c0000 0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
  //   contents of rom_27 (hex, n*v repeats v):
  //   0 e00000 6600000 5*0 1000 0 0 c3000 5*0 300 1800000 60 c000000 330 cc00000 1800 100000 1a00 fd80000
  //   18180 3818000 1ff80 1ff0000 0 80 38000 38000 6000060 3c000 1ffff80 1c00380 7c000 1800180 0 1800380
  //   e000 18000 6030000 7000000 0 f00f00 330000 3b0000 0 ffffff0 0 0 0 c00000 30000 c000 7e0 3e00000 0
  //   3c0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
  //   contents of rom_28 (hex, n*v repeats v):
  //   0 600000 3c00000 8*0 c3000 5*0 180 3000000 60 c000000 330 18c00000 1800 100000 1a00 fd80000 180c0
  //   3018000 1ff80 3ff0000 7ffffe0 0 0 0 6000060 1c000 3ffff80 ff01ff0 4*0 4000 ffffff0 6030000 fffffe0 0
  //   3ffc00 330000 3f0000 5*0 400000 30000 c000 f0 7000000 0 0 0 1ff800 18000 0 0 0 1fc00 dff800 c1ff830
  //   1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
  //   contents of rom_29 (hex, n*v repeats v):
  //   0 600000 1000000 8*0 c3000 5*0 c0 6000000 30 18000000 198 19800000 1800 100000 1a00 c180000 18060
  //   7ff8000 1ffc0 7ff0000 7ffffe0 0 0 0 c000030 18000 7ffff80 ff01ff0 9*0 ff000 3e0000 3e0000 6*0 30000
  //   c000 10 4*0 fe000 18000 4*0 7e000 18018010 0 0 3c0f0 1c7000 0 1800180 1800180 7e000 3c000 3c000
  //   18000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
  //   contents of rom_30 (hex, n*v repeats v):
  //   11*0 c3000 5*0 40 0 10 8000000 108 10800000 1800 ff00000 1e00 ff80000 1fff0 fff8000 1ffe0 7ff0000
  //   4*0 20 8000 12*0 80000 14*0 18000 5*0 18000 4*0 fe000 0 1000080 1000080 12*0 18000 58*0 f00700
  //   9*e00f00 39*0 8000000 0 0 200000 11*0 3000000 4*0 1ffc00 16*0 700 9*0 7ff0 380 7fe0000 9*0 3ff800 0
  //   0 ff000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
  //   contents of rom_31 (hex, n*v repeats v):
  //   24*0 7f00000 e00 7f00000 0 0 ffe0 7fe0000 119*0 10*3ffc00 54*0 6000000 4*0 3c000 26*0 7ff0 0 ffe0000
  //   9*0 1fe000 0 0 7e0000 5*0 7e0000 7f00 7*0 3c0000 0 0 10000 271*0 38000 0 60000000 70000000 77*0
  //   300000 56*0 38700000 22*0 80000 44*0 3c000 3c000 0 0 3c000 3c000 0 0 10*3c000 8*0 24*3c000 8*0
  //   16*3c000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
  //   contents of rom_32 (hex, n*v repeats v):
  //   150*0 10*7e000 88*0 7fc0000 0 ffffffff 16*0 7e0000 3e00 282*0 10000 0 60000000 70000000 134*0
  //   1fe00000 67*0 3c000 3c000 0 0 3c000 3c000 0 0 10*3c000 8*0 24*3c000 8*0 16*3c000 25*0 3c00 fc0ffff
  //   556*0 1000000 11*0 4 17*0 800000 800000 10*0 80000 4*0 400000 29*0 200000 20*0 20000 0 0 2000 19*0
  //   40000 22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
endmodule
